# Fritzing sketch sensors_layout (saved by Fritzing 0.8.7b)
breadboards: 1

parts:
  Parte1 = Arduino Uno (Rev3)
  RHT1 = Humidity and Temperature Sensor RHT03
  Wind_vane = VARISTOR [package=0402-res]
  Tipping_bucket_gauge_switch = SWITCH-MOMENTARY-2 [package=tactile_switch_smd-2]
  Cup_anemometer_switch = SWITCH-MOMENTARY-2 [package=tactile_switch_smd-2]
  R1 = Resistor [package="2010 [SMD]"]
  R2 = Resistor [package="2010 [SMD]"]
  C1 = Ceramic Capacitor [capacitance=0.1mF package="100 mil [THT, multilayer]"]
  R3 = Resistor [package="2010 [SMD]"]
  Parte2 = Barometric Pressure Sensor - BMP085 Breakout
  A1 = PMS5003

nets:
  N1: Parte1.A0, Wind_vane.2, R3.Pin_0
  GND: Parte1.GND, RHT1.GND_2, Wind_vane.1, Cup_anemometer_switch.1, Parte2.GND, A1.Pin_2
  N2: Parte1.A4/SDA, Parte2.SDA
  N3: Parte1.A5/SCL, Parte2.SCL
  N4: Parte1.D2, Tipping_bucket_gauge_switch.2, R2.Pin_0, C1.0
  N5: Parte1.D3_PWM, Cup_anemometer_switch.2, R1.Pin_0
  N6: Parte1.D4, RHT1.Data-signal
  5V: Parte1.5V, R3.Pin_1, Parte2.VCC, A1.Pin_1
  5V_2: Parte1.VIN
  N7: RHT1.Vcc, R1.Pin_1, R2.Pin_1
  N8: Tipping_bucket_gauge_switch.1, C1.1

notes:
  Arduino Weather Station, Hookup layour for Arduino UNO and wind, rain, temperature, humidity and pressure sensors., 1.0

custom parts:
  Resistor: Resistor Basic schematic elements and footprints for 0603, 1206, and PTH resistors.
  PMS5003: PMS5003 is a kind of digital and universal particle concentration sensor, which can be used to obtain the number of suspended particles in the air.
